// Logisim project alu.circ as structural Verilog: 1 circuit, main circuit alu
module alu (
  input  [31:0] A,
  input  [31:0] B,
  input  [3:0] ALUSel,
  output [31:0] Result
);

  wire comparator_1_lt;
  wire [31:0] add0, and0, bit_extender_1_out, bit_extender_2_out, bit_extender_3_out, bit_extender_4_out,
       bit_extender_5_out, bit_extender_6_out, bit_extender_7_out, bit_extender_8_out, bit_extender_10_out,
       bit_extender_11_out, mul0, mulh0, mulhu0, multiplexer_1_out, multiplexer_2_out, multiplexer_3_out,
       multiplexer_4_out, multiplexer_5_out, multiplexer_6_out, multiplexer_8_out, multiplexer_9_out,
       multiplexer_10_out, multiplexer_11_out, multiplexer_12_out, multiplexer_13_out, or0, sll0, slt0, sra0,
       srl0, sub0, xor0;

  Multiplier #(.width(32)) multiplier_1 (.a(A), .b(B), .out(mul0), .cout(mulhu0));  // open: cin
  Multiplier #(.mode("twosComplement"), .width(32)) multiplier_2 (.a(A), .b(B), .cout(mulh0));  // open: out, cin
  assign bit_extender_1_out = {{1{1'b0}}, A[31:1]};  // Bit_Extender bit_extender_1
  assign bit_extender_2_out = {{1{A[31]}}, A[31:1]};  // Bit_Extender bit_extender_2
  Multiplexer #(.enable("false"), .width(32)) multiplexer_1 (
    .in0(A), .in1(bit_extender_1_out), .out(multiplexer_1_out), .sel(B[0]));
  Multiplexer #(.enable("false"), .width(32)) multiplexer_2 (
    .in0(A), .in1(bit_extender_2_out), .out(multiplexer_2_out), .sel(B[0]));
  Multiplexer #(.enable("false"), .width(32)) multiplexer_3 (
    .in0(A), .in1({A[30:0], 1'b0}), .out(multiplexer_3_out), .sel(B[0]));
  Multiplexer #(.enable("false"), .width(32)) multiplexer_4 (
    .in0(multiplexer_1_out), .in1(bit_extender_3_out), .out(multiplexer_4_out), .sel(B[1]));
  assign bit_extender_3_out = {{2{1'b0}}, multiplexer_1_out[31:2]};  // Bit_Extender bit_extender_3
  Multiplexer #(.enable("false"), .width(32)) multiplexer_5 (
    .in0(multiplexer_2_out), .in1(bit_extender_4_out), .out(multiplexer_5_out), .sel(B[1]));
  assign bit_extender_4_out = {{2{multiplexer_2_out[31]}}, multiplexer_2_out[31:2]};  // Bit_Extender bit_extender_4
  Multiplexer #(.enable("false"), .width(32)) multiplexer_6 (
    .in0(multiplexer_3_out), .in1({multiplexer_3_out[29:0], 2'b00}), .out(multiplexer_6_out), .sel(B[1]));
  Multiplexer #(.enable("false"), .select(4), .width(32)) multiplexer_7 (
    .in0(add0), .in1(and0), .in2(or0), .in3(xor0), .in4(srl0), .in5(sra0), .in6(sll0), .in7(slt0),
    .in10(mul0), .in11(mulhu0), .in12(sub0), .in13(B), .in14(mulh0), .out(Result), .sel(ALUSel));  // open: in8, in9, in15
  Multiplexer #(.enable("false"), .width(32)) multiplexer_8 (
    .in0(multiplexer_4_out), .in1(bit_extender_5_out), .out(multiplexer_8_out), .sel(B[2]));
  assign bit_extender_5_out = {{4{1'b0}}, multiplexer_4_out[31:4]};  // Bit_Extender bit_extender_5
  Multiplexer #(.enable("false"), .width(32)) multiplexer_9 (
    .in0(multiplexer_5_out), .in1(bit_extender_6_out), .out(multiplexer_9_out), .sel(B[2]));
  assign bit_extender_6_out = {{4{multiplexer_5_out[31]}}, multiplexer_5_out[31:4]};  // Bit_Extender bit_extender_6
  Multiplexer #(.enable("false"), .width(32)) multiplexer_10 (
    .in0(multiplexer_6_out), .in1({multiplexer_6_out[27:0], 4'b0000}), .out(multiplexer_10_out), .sel(B[2]));
  assign bit_extender_7_out = {{8{1'b0}}, multiplexer_8_out[31:8]};  // Bit_Extender bit_extender_7
  assign bit_extender_8_out = {{8{multiplexer_9_out[31]}}, multiplexer_9_out[31:8]};  // Bit_Extender bit_extender_8
  Comparator #(.width(32)) comparator_1 (.a(A), .b(B), .lt(comparator_1_lt));  // open: gt, eq
  Adder #(.width(32)) adder_1 (.a(A), .b(B), .out(add0));  // open: cin, cout
  Subtractor #(.width(32)) subtractor_1 (.a(A), .b(B), .out(sub0));  // open: bin, bout
  assign and0 = A & B;  // AND_Gate and_1, 32 bits wide
  assign or0 = A | B;  // OR_Gate or_1, 32 bits wide
  assign xor0 = A ^ B;  // XOR_Gate xor_1, 32 bits wide
  Multiplexer #(.enable("false"), .width(32)) multiplexer_11 (
    .in0(multiplexer_8_out), .in1(bit_extender_7_out), .out(multiplexer_11_out), .sel(B[3]));
  Multiplexer #(.enable("false"), .width(32)) multiplexer_12 (
    .in0(multiplexer_9_out), .in1(bit_extender_8_out), .out(multiplexer_12_out), .sel(B[3]));
  Multiplexer #(.enable("false"), .width(32)) multiplexer_13 (
    .in0(multiplexer_10_out), .in1({multiplexer_10_out[23:0], {8{1'b0}}}), .out(multiplexer_13_out),
    .sel(B[3]));
  assign slt0 = {{31{1'b0}}, comparator_1_lt};  // Bit_Extender bit_extender_9
  assign bit_extender_10_out = {{16{1'b0}}, multiplexer_11_out[31:16]};  // Bit_Extender bit_extender_10
  assign bit_extender_11_out = {{16{multiplexer_12_out[31]}}, multiplexer_12_out[31:16]};  // Bit_Extender bit_extender_11
  Multiplexer #(.enable("false"), .width(32)) multiplexer_14 (
    .in0(multiplexer_11_out), .in1(bit_extender_10_out), .out(srl0), .sel(B[4]));
  Multiplexer #(.enable("false"), .width(32)) multiplexer_15 (
    .in0(multiplexer_12_out), .in1(bit_extender_11_out), .out(sra0), .sel(B[4]));
  Multiplexer #(.enable("false"), .width(32)) multiplexer_16 (
    .in0(multiplexer_13_out), .in1({multiplexer_13_out[15:0], {16{1'b0}}}), .out(sll0), .sel(B[4]));

  // Notes on the sheet:
  //   INPUTS to your circuit
  //   DON'T CHANGE THE LOCATIONS OF THE INPUTS AND OUTPUTS!
  //   OUTPUT from your circuit
endmodule
