// Logisim project control_logic.circ as structural Verilog: 1 circuit, main circuit control_logic
module control_logic (
  input  [31:0] inst,
  input  BrEq,
  input  BrLt,
  output PCSel,
  output RegWEn,
  output [2:0] ImmSel,
  output BrUn,
  output ASel,
  output BSel,
  output [3:0] ALUSel,
  output MemRW,
  output [1:0] WBSel,
  output CSRSel,
  output CSRWen
);

  wire comparator_2_eq, comparator_3_eq, comparator_4_eq, comparator_5_eq, multiplexer_16_out, not_1_out,
       not_2_out, not_3_out;
  wire [2:0] multiplexer_5_out, multiplexer_7_out, multiplexer_8_out;
  wire [3:0] ALUSel_I, ALUSel_R, multiplexer_1_out, multiplexer_2_out, multiplexer_3_out, multiplexer_4_out,
       multiplexer_6_out, multiplexer_13_out;

  Multiplexer #(.enable("false"), .width(4)) multiplexer_1 (
    .in0(4'b0000), .in1(4'b1100), .out(multiplexer_1_out), .sel(inst[30]));
  Multiplexer #(.enable("false"), .width(4)) multiplexer_2 (
    .in0(4'b0110), .in1(4'b1110), .out(multiplexer_2_out), .sel(inst[26]));
  Multiplexer #(.enable("false"), .width(4)) multiplexer_3 (
    .in0(4'b0100), .in1(4'b0101), .out(multiplexer_3_out), .sel(inst[30]));
  Multiplexer #(.enable("false"), .width(4)) multiplexer_4 (
    .in0(4'b0100), .in1(4'b0101), .out(multiplexer_4_out), .sel(inst[30]));
  Multiplexer #(.enable("false"), .width(3)) multiplexer_5 (
    .in0(3'b000), .in1(3'b101), .out(multiplexer_5_out), .sel(inst[2]));
  Multiplexer #(.enable("false"), .width(4)) multiplexer_6 (
    .in0(multiplexer_1_out), .in1(4'b1010), .out(multiplexer_6_out), .sel(inst[26]));
  Multiplexer #(.enable("false"), .width(3)) multiplexer_7 (
    .in0(3'b001), .in1(3'b101), .out(multiplexer_7_out), .sel(inst[2]));
  Multiplexer #(.enable("false"), .select(2), .width(3)) multiplexer_8 (
    .in0(3'b011), .in1(3'b001), .in3(3'b100), .out(multiplexer_8_out), .sel(inst[3:2]));  // open: in2
  Multiplexer #(.enable("false"), .select(3), .width(4)) multiplexer_9 (
    .in0(4'b0000), .in1(4'b0110), .in2(4'b0111), .in4(4'b0011), .in5(multiplexer_4_out), .in6(4'b0010),
    .in7(4'b0001), .out(ALUSel_I), .sel(inst[14:12]));  // open: in3
  Multiplexer #(.enable("false"), .select(3), .width(3)) multiplexer_10 (
    .in0(3'b001), .in1(multiplexer_7_out), .in2(3'b010), .in3(multiplexer_5_out), .in6(multiplexer_8_out),
    .in7(3'b110), .out(ImmSel), .sel(inst[6:4]));  // open: in4, in5
  Multiplexer #(.enable("false"), .select(3)) multiplexer_11 (
    .in0(1'b0), .in1(1'b0), .in2(1'b0), .in3(1'b0), .in4(1'b0), .in5(1'b0), .in6(1'b1), .in7(1'b1),
    .out(BrUn), .sel(inst[14:12]));
  Multiplexer #(.enable("false"), .select(3), .width(4)) multiplexer_12 (
    .in0(multiplexer_6_out), .in1(multiplexer_2_out), .in2(4'b0111), .in3(4'b1011), .in4(4'b0011),
    .in5(multiplexer_3_out), .in6(4'b0010), .in7(4'b0001), .out(ALUSel_R), .sel(inst[14:12]));
  not not_1 (not_1_out, 1'b1);
  Multiplexer #(.enable("false"), .width(4)) multiplexer_13 (
    .in0(4'b0000), .in1(4'b1101), .out(multiplexer_13_out), .sel(inst[5]));
  Multiplexer #(.enable("false"), .select(3)) multiplexer_14 (
    .in0(1'b1), .in1(1'b1), .in2(not_1_out), .in3(not_1_out), .in4(1'b1), .in5(1'b1), .in6(not_1_out),
    .out(RegWEn), .sel(ImmSel));  // open: in7
  not not_2 (not_2_out, BrLt);
  Multiplexer #(.enable("false"), .select(3), .width(4)) multiplexer_15 (
    .in0(ALUSel_R), .in1(ALUSel_I), .in2(4'b0000), .in3(4'b0000), .in4(4'b0000), .in5(multiplexer_13_out),
    .out(ALUSel), .sel(ImmSel));  // open: in6, in7
  not not_3 (not_3_out, BrEq);
  Multiplexer #(.enable("false"), .select(3)) multiplexer_16 (
    .in0(BrEq), .in1(not_3_out), .in4(BrLt), .in5(not_2_out), .in6(BrLt), .in7(not_2_out),
    .out(multiplexer_16_out), .sel(inst[14:12]));  // open: in2, in3
  Comparator #(.mode("unsigned"), .width(7)) comparator_1 (.a(inst[6:0]), .b(7'b1110011), .eq(CSRWen));  // open: gt, lt
  Multiplexer #(.enable("false"), .select(3)) multiplexer_17 (
    .in0(1'b0), .in1(inst[2]), .in2(1'b0), .in3(multiplexer_16_out), .in4(1'b1), .in5(1'b0), .in6(1'b0),
    .out(PCSel), .sel(ImmSel));  // open: in7
  not not_4 (BSel, comparator_2_eq);
  Comparator #(.mode("unsigned"), .width(3)) comparator_2 (
    .a(ImmSel), .b(3'b000), .eq(comparator_2_eq));  // open: gt, lt
  Comparator #(.mode("unsigned"), .width(7)) comparator_3 (
    .a(inst[6:0]), .b(7'b0010111), .eq(comparator_3_eq));  // open: gt, lt
  Comparator #(.mode("unsigned"), .width(7)) comparator_4 (
    .a(inst[6:0]), .b(7'b1101111), .eq(comparator_4_eq));  // open: gt, lt
  Comparator #(.mode("unsigned"), .width(7)) comparator_5 (
    .a(inst[6:0]), .b(7'b1100011), .eq(comparator_5_eq));  // open: gt, lt
  Comparator #(.width(3)) comparator_6 (.a(inst[6:4]), .b(3'b010), .eq(MemRW));  // open: gt, lt
  Multiplexer #(.enable("false"), .select(3), .width(2)) multiplexer_18 (
    .in0(2'b01), .in1(2'b00), .in2(2'b00), .in3(2'b00), .in4(2'b00), .in5(2'b00), .in6(2'b10), .in7(2'b00),
    .out(WBSel), .sel(inst[6:4]));
  or or_1 (ASel, comparator_3_eq, comparator_4_eq, comparator_5_eq);

  assign CSRSel = inst[14];

  // Other names for the same wires on the sheet: opcode[6:0] = inst[6:0]; op_low[1:0] = inst[3:2]; opcode_2 = inst[2];
  //   op_high[2:0] = inst[6:4]; opcode_5 = inst[5]; func3[2:0] = inst[14:12]; func7_2 = inst[26]; func7_6 = inst[30]

  // Notes on the sheet:
  //   INPUTS to your circuit
  //   DON'T CHANGE THE LOCATIONS OF THE INPUTS AND OUTPUTS!
  //   OUTPUT from your circuit
endmodule
