// Logisim project cpu.circ as structural Verilog: 1 circuit, main circuit cpu
module cpu (
  input  clk,
  input  [31:0] INSTRUCTION,
  input  [31:0] READ_DATA,
  output [31:0] WRITE_ADDRESS,
  output [31:0] PROGRAM_COUNTER,
  output [31:0] ra,
  output [31:0] sp,
  output [31:0] t0,
  output [31:0] t1,
  output [31:0] t2,
  output [31:0] s0,
  output [31:0] s1,
  output [31:0] a0,
  output [31:0] tohost,
  output [3:0] WRITE_ENABLE,
  output [31:0] WRITE_DATA
);

  wire ASel, BrEq, BrLt, BrUn, BSel, CSRSel, CSRWen, MemRW, PCSel, RegWEn;
  wire [1:0] WBSel;
  wire [2:0] ImmSel;
  wire [3:0] ALUSel, multiplexer_9_out, multiplexer_10_out;
  wire [7:0] multiplexer_7_out;
  wire [15:0] multiplexer_8_out;
  wire [31:0] adder_1_out, adder_2_out, bit_extender_1_out, bit_extender_2_out, bit_extender_3_out, Imm,
       inst_reg, mem_read_data, multiplexer_1_out, multiplexer_2_out, multiplexer_3_out, multiplexer_4_out,
       multiplexer_5_out, multiplexer_6_out, pc_reg, read_data1;

  Register #(.width(32)) register_1 (.D(multiplexer_1_out), .en(1'b1), .clk(clk), .Q(inst_reg));  // open: clr
  Multiplexer #(.enable("false"), .width(32)) multiplexer_1 (
    .in0(INSTRUCTION), .in1(32'h13), .out(multiplexer_1_out), .sel(PCSel));
  Register #(.width(32)) register_2 (.D(PROGRAM_COUNTER), .en(1'b1), .clk(clk), .Q(pc_reg));  // open: clr
  imm_gen imm_gen_1 (.inst(inst_reg), .ImmSel(ImmSel), .imm(Imm));
  Adder #(.width(32)) adder_1 (.a(pc_reg), .b(32'h4), .out(adder_1_out));  // open: cin, cout
  control_logic control_logic_1 (
    .CSRWen(CSRWen), .PCSel(PCSel), .RegWEn(RegWEn), .ImmSel(ImmSel), .BrUn(BrUn), .ASel(ASel), .BSel(BSel),
    .ALUSel(ALUSel), .MemRW(MemRW), .WBSel(WBSel), .CSRSel(CSRSel), .inst(inst_reg), .BrEq(BrEq), .BrLt(BrLt));
  Multiplexer #(.enable("false"), .select(2), .width(32)) multiplexer_2 (
    .in0(WRITE_ADDRESS), .in1(mem_read_data), .in2(adder_1_out), .out(multiplexer_2_out), .sel(WBSel));  // open: in3
  regfile regfile_1 (
    .rs1(inst_reg[19:15]), .rs2(inst_reg[24:20]), .rd(inst_reg[11:7]), .Write_Data(multiplexer_2_out),
    .RegWEn(RegWEn), .clk(clk), .ra(ra), .sp(sp), .t0(t0), .t1(t1), .t2(t2), .s0(s0), .s1(s1), .a0(a0),
    .Read_Data_1(read_data1), .Read_Data_2(WRITE_DATA));
  Adder #(.width(32)) adder_2 (.a(PROGRAM_COUNTER), .b(32'h4), .out(adder_2_out));  // open: cin, cout
  Multiplexer #(.enable("false"), .width(32)) multiplexer_3 (
    .in0(adder_2_out), .in1(WRITE_ADDRESS), .out(multiplexer_3_out), .sel(PCSel));
  branch_comp branch_comp_1 (.rs1(read_data1), .rs2(WRITE_DATA), .BrUn(BrUn), .BrEq(BrEq), .BrLt(BrLt));
  Register #(.width(32)) PC (.D(multiplexer_3_out), .clk(clk), .Q(PROGRAM_COUNTER));  // open: en, clr
  Multiplexer #(.enable("false"), .width(32)) multiplexer_4 (
    .in0(read_data1), .in1(pc_reg), .out(multiplexer_4_out), .sel(ASel));
  Multiplexer #(.enable("false"), .width(32)) multiplexer_5 (
    .in0(WRITE_DATA), .in1(Imm), .out(multiplexer_5_out), .sel(BSel));
  alu alu_1 (.Result(WRITE_ADDRESS), .A(multiplexer_4_out), .B(multiplexer_5_out), .ALUSel(ALUSel));
  assign bit_extender_1_out = {{27{1'b0}}, inst_reg[19:15]};  // Bit_Extender bit_extender_1
  Multiplexer #(.enable("false"), .width(32)) multiplexer_6 (
    .in0(read_data1), .in1(bit_extender_1_out), .out(multiplexer_6_out), .sel(CSRSel));
  Multiplexer #(.enable("false"), .select(2), .width(8)) multiplexer_7 (
    .in0(READ_DATA[7:0]), .in1(READ_DATA[15:8]), .in2(READ_DATA[23:16]), .in3(READ_DATA[31:24]),
    .out(multiplexer_7_out), .sel(WRITE_ADDRESS[1:0]));
  Multiplexer #(.enable("false"), .width(16)) multiplexer_8 (
    .in0(READ_DATA[15:0]), .in1(READ_DATA[31:16]), .out(multiplexer_8_out), .sel(WRITE_ADDRESS[1]));
  assign bit_extender_2_out = {{24{multiplexer_7_out[7]}}, multiplexer_7_out};  // Bit_Extender bit_extender_2
  assign bit_extender_3_out = {{16{multiplexer_8_out[15]}}, multiplexer_8_out};  // Bit_Extender bit_extender_3
  Multiplexer #(.enable("false"), .width(4)) multiplexer_9 (
    .in0(4'b0011), .in1(4'b1100), .out(multiplexer_9_out), .sel(WRITE_ADDRESS[1]));
  Multiplexer #(.enable("false"), .select(2), .width(4)) multiplexer_10 (
    .in0(4'b0001), .in1(4'b0010), .in2(4'b0100), .in3(4'b1000), .out(multiplexer_10_out),
    .sel(WRITE_ADDRESS[1:0]));
  Multiplexer #(.enable("false"), .select(2), .width(32)) multiplexer_11 (
    .in0(bit_extender_2_out), .in1(bit_extender_3_out), .in2(READ_DATA), .out(mem_read_data),
    .sel(inst_reg[13:12]));  // open: in3
  csr csr_1 (.CSR_address(inst_reg[31:20]), .CSR_din(multiplexer_6_out), .CSR_WE(CSRWen), .clk(clk), .tohost(tohost));
  Multiplexer #(.enable("false"), .select(2), .width(4)) multiplexer_12 (
    .in0(multiplexer_10_out), .in1(multiplexer_9_out), .in2(4'b1111), .out(WRITE_ENABLE),
    .sel(inst_reg[13:12]));  // open: in3

  // Other names for the same wires on the sheet: ALU_output[31:0] = WRITE_ADDRESS; low_bits[1:0] = WRITE_ADDRESS[1:0];
  //   rd[4:0] = inst_reg[11:7]; rs1[4:0] = inst_reg[19:15]; rs2[4:0] = inst_reg[24:20]; read_data2[31:0] = WRITE_DATA

  // Notes on the sheet:
  //   Output to IMEM
  //   IMEM (do **NOT** move this)
  //   Inputs from IMEM
  //   It is OK to move the PC, RegFile, ALU, MEM, Branch Comp, Imm Gen, and Control Logic to wherever is most convenient for you when constructing your CPU, and to delete this text
  //   Inputs/Outputs for testing. Do **NOT** move these.
  //   Outputs To DMEM
  //   DMEM (do **NOT** move this)
  //   Inputs From DMEM
endmodule
