// Logisim project imm_gen.circ as structural Verilog: 1 circuit, main circuit imm_gen
module imm_gen (
  input  [31:0] inst,
  input  [2:0] ImmSel,
  output [31:0] imm
);

  wire [30:0] bit_extender_4_out;
  wire [31:0] bit_extender_1_out, bit_extender_2_out, bit_extender_3_out;

  assign bit_extender_1_out = {{20{inst[31]}}, inst[31:20]};  // Bit_Extender bit_extender_1
  assign bit_extender_2_out = {{11{inst[31]}}, {inst[31], inst[19:12], inst[20], inst[30:21], 1'b0}};  // Bit_Extender bit_extender_2
  assign bit_extender_3_out = {{20{inst[31]}}, {inst[31:25], inst[11:7]}};  // Bit_Extender bit_extender_3
  assign bit_extender_4_out = {{19{inst[31]}}, {inst[31], inst[7], inst[30:25], inst[11:8]}};  // Bit_Extender bit_extender_4
  Multiplexer #(.enable("false"), .select(3), .width(32)) multiplexer_1 (
    .in1(bit_extender_1_out), .in2(bit_extender_3_out), .in3({bit_extender_4_out, 1'b0}),
    .in4(bit_extender_2_out), .in5({inst[31:12], {12{1'b0}}}), .out(imm), .sel(ImmSel));  // open: in0, in6, in7

  // Notes on the sheet:
  //   INPUTS to your circuit
  //   DON'T CHANGE THE LOCATIONS OF THE INPUTS AND OUTPUTS!
  //   OUTPUT from your circuit
endmodule
